// Logisim project one instruction cpu.circ as structural Verilog
module main (
);

  wire alu_1_leq_zero, Bootlaoder_unlock_system, Bootlaoder_write_ram, button_1_out, clock_1_out,
       decoder_1_mem_addr, decoder_1_save_result, decoder_1_value_1, decoder_1_value_2, not_1_out, or_1_out,
       pc_1_new_instruction;
  wire [15:0] adder_1_out, alu_1_out_6, Bootlaoder_address, Bootlaoder_data, Bootlaoder_prog_length,
       counter_1_q, decoder_1_out_5, memory_1_data_out, multiplexer_1_out, multiplexer_2_out,
       multiplexer_3_out, pc_1_counter, sub_instruction_counter_1_sub_address;

  Counter #(.width(16), .max('hffff)) counter_1 (
    .load(1'b0), .count(1'b1), .Q(counter_1_q), .clk(clock_1_out), .clr(button_1_out));  // open: D, carry
  Clock clock_1 (.out(clock_1_out));
  Button button_1 (.out(button_1_out));
  Hex_Digit_Display hex_digit_display_1 (.value(counter_1_q[11:8]));  // open: dp
  Hex_Digit_Display hex_digit_display_2 (.value(counter_1_q[15:12]));  // open: dp
  Hex_Digit_Display hex_digit_display_3 (.value(counter_1_q[7:4]));  // open: dp
  Hex_Digit_Display hex_digit_display_4 (.value(counter_1_q[3:0]));  // open: dp
  pc pc_1 (
    .address(decoder_1_out_5), .jump(alu_1_leq_zero), .clock(clock_1_out), .reset(button_1_out),
    .lock(not_1_out), .Counter(pc_1_counter), .New_instruction(pc_1_new_instruction));
  sub_instruction_counter sub_instruction_counter_1 (
    .new_instruction(pc_1_new_instruction), .clock(clock_1_out), .clear(button_1_out), .lock(not_1_out),
    .sub_address(sub_instruction_counter_1_sub_address));
  Adder #(.width(16)) adder_1 (
    .a(pc_1_counter), .b(sub_instruction_counter_1_sub_address), .out(adder_1_out));  // open: cin, cout
  decoder decoder_1 (
    .data(memory_1_data_out), .sub_instruction(sub_instruction_counter_1_sub_address), .clock(clock_1_out),
    .reset(button_1_out), .out_5(decoder_1_out_5), .mem_addr(decoder_1_mem_addr),
    .save_result(decoder_1_save_result), .value_1(decoder_1_value_1), .value_2(decoder_1_value_2));
  not not_1 (not_1_out, Bootlaoder_unlock_system);
  Multiplexer #(.width(16), .enable("false")) multiplexer_1 (
    .in0(adder_1_out), .in1(decoder_1_out_5), .out(multiplexer_1_out), .sel(decoder_1_mem_addr));
  Multiplexer #(.width(16), .enable("false")) multiplexer_2 (
    .in0(Bootlaoder_address), .in1(multiplexer_1_out), .out(multiplexer_2_out), .sel(Bootlaoder_unlock_system));
  bootloader Bootlaoder (
    .clock(clock_1_out), .reset(button_1_out), .Address(Bootlaoder_address), .Data(Bootlaoder_data),
    .Write_ram(Bootlaoder_write_ram), .unlock_system(Bootlaoder_unlock_system),
    .Prog_Length(Bootlaoder_prog_length));
  Multiplexer #(.width(16), .enable("false")) multiplexer_3 (
    .in0(Bootlaoder_data), .in1(alu_1_out_6), .out(multiplexer_3_out), .sel(Bootlaoder_unlock_system));
  or or_1 (or_1_out, decoder_1_save_result, Bootlaoder_write_ram);
  special_function_registers special_function_registers_1 (
    .Prog_Length(Bootlaoder_prog_length), .address(multiplexer_2_out), .data_in(multiplexer_3_out),
    .clock(clock_1_out), .write_nread(or_1_out), .reset(button_1_out), .Running(Bootlaoder_unlock_system));
  memory memory_1 (
    .address(multiplexer_2_out), .clock(clock_1_out), .write_nread(or_1_out), .reset(button_1_out),
    .data_in(multiplexer_3_out), .data_out(memory_1_data_out));
  alu alu_1 (
    .in_1(memory_1_data_out), .value_1(decoder_1_value_1), .value_2(decoder_1_value_2), .clock(clock_1_out),
    .reset(button_1_out), .out_6(alu_1_out_6), .LEQ_zero(alu_1_leq_zero));

  // Notes on the sheet:
  //   Clock Cycles
endmodule

module clock_divider (
  input  clock_in,
  input  [15:0] divide_by,
  input  reset,
  input  lock,
  output clock_out
);

  wire [15:0] adder_1_out, multiplexer_1_out, multiplexer_2_out, register_1_q;

  Multiplexer #(.width(16), .enable("false")) multiplexer_1 (
    .in0(multiplexer_2_out), .in1({16{1'b0}}), .out(multiplexer_1_out), .sel(lock));
  Register #(.width(16)) register_1 (.D(multiplexer_1_out), .Q(register_1_q), .clk(clock_in), .clr(reset));  // open: en
  Adder #(.width(16)) adder_1 (.a(register_1_q), .b(16'h1), .out(adder_1_out));  // open: cin, cout
  Multiplexer #(.width(16), .enable("false")) multiplexer_2 (
    .in0(adder_1_out), .in1(16'h1), .out(multiplexer_2_out), .sel(clock_out));
  Comparator #(.width(16)) comparator_1 (.a(register_1_q), .b(divide_by), .eq(clock_out));  // open: gt, lt
endmodule

// PC
module pc (
  input  [15:0] address,
  input  jump,
  input  clock,
  input  reset,
  input  lock,
  output [15:0] Counter,
  output New_instruction
);

  wire [15:0] adder_1_out, multiplexer_1_out;

  Multiplexer #(.width(16), .enable("false")) multiplexer_1 (
    .in0(adder_1_out), .in1(address), .out(multiplexer_1_out), .sel(jump));
  Register #(.width(16)) register_1 (
    .D(multiplexer_1_out), .Q(Counter), .clk(New_instruction), .clr(reset));  // open: en
  clock_divider clock_divider_1 (
    .clock_in(clock), .divide_by(16'h7), .reset(reset), .lock(lock), .clock_out(New_instruction));
  Adder #(.width(16)) adder_1 (.a(Counter), .b(16'h3), .out(adder_1_out));  // open: cin, cout

  // Notes on the sheet:
  //   stages
  //   instruction size
endmodule

// RAM
module memory (
  input  [15:0] address,
  input  clock,
  input  write_nread,
  input  reset,
  input  [15:0] data_in,
  output [15:0] data_out
);

  wire not_1_out;
  wire [15:0] multiplexer_1_out, undriven;

  not not_1 (not_1_out, write_nread);
  RAM #(.addrWidth(16), .dataWidth(16)) ram_1 (
    .addr(address), .data(data_out), .sel(1'b1), .clk(clock), .ld(not_1_out), .clr(reset));
  Multiplexer #(.width(16)) multiplexer_1 (
    .in0(data_in), .in1(undriven), .out(multiplexer_1_out), .sel(not_1_out));  // open: en
  assign data_out = multiplexer_1_out;  // Buffer buffer_1, 16 bits wide
endmodule

module sub_instruction_counter (
  input  new_instruction,
  input  clock,
  input  clear,
  input  lock,
  output [15:0] sub_address
);

  wire [15:0] adder_1_out, multiplexer_1_out, multiplexer_2_out, register_1_q;

  Multiplexer #(.width(16), .enable("false")) multiplexer_1 (
    .in0(adder_1_out), .in1(16'h1), .out(multiplexer_1_out), .sel(new_instruction));
  Multiplexer #(.width(16), .enable("false")) multiplexer_2 (
    .in0(multiplexer_1_out), .in1({16{1'b0}}), .out(multiplexer_2_out), .sel(lock));
  Register #(.width(16)) register_1 (.D(multiplexer_2_out), .Q(register_1_q), .clk(clock), .clr(clear));  // open: en
  Adder #(.width(16)) adder_1 (.a(register_1_q), .b(16'h1), .out(adder_1_out));  // open: cin, cout
  Subtractor #(.width(16)) subtractor_1 (.a(multiplexer_2_out), .b(16'h1), .out(sub_address));  // open: bin, bout
endmodule

// ALU
module alu (
  input  [15:0] in_1,
  input  value_1,
  input  value_2,
  input  clock,
  input  reset,
  output [15:0] out_6,
  output LEQ_zero
);

  wire leq_zero_1_out_2, register_3_q;
  wire [15:0] multiplexer_1_out, multiplexer_2_out, register_1_q, register_2_q;

  Multiplexer #(.width(16), .enable("false")) multiplexer_1 (
    .in0(register_1_q), .in1(in_1), .out(multiplexer_1_out), .sel(value_1));
  Multiplexer #(.width(16), .enable("false")) multiplexer_2 (
    .in0(register_2_q), .in1(in_1), .out(multiplexer_2_out), .sel(value_2));
  Register #(.width(16)) register_1 (.D(multiplexer_1_out), .Q(register_1_q), .clk(clock), .clr(reset));  // open: en
  Register #(.width(16)) register_2 (.D(multiplexer_2_out), .Q(register_2_q), .clk(clock), .clr(reset));  // open: en
  Subtractor #(.width(16)) subtractor_1 (.a(register_1_q), .b(register_2_q), .out(out_6));  // open: bin, bout
  LEQ_zero leq_zero_1 (.in_1(out_6), .out_2(leq_zero_1_out_2));
  Register #(.width(1)) register_3 (.D(leq_zero_1_out_2), .Q(register_3_q), .clk(clock), .clr(reset));  // open: en
  Register #(.width(1)) register_4 (.D(register_3_q), .Q(LEQ_zero), .clk(clock), .clr(reset));  // open: en
endmodule

// DECODER
module decoder (
  input  [15:0] data,
  input  [15:0] sub_instruction,
  input  clock,
  input  reset,
  output [15:0] out_5,
  output mem_addr,
  output save_result,
  output value_1,
  output value_2
);

  wire comparator_1_eq, comparator_2_eq, comparator_3_eq, comparator_6_eq;
  wire [15:0] and_1_out, and_2_out, and_3_out, and_4_out, and_5_out, and_6_out, and_7_out, Jump_to_reg_q,
       multiplexer_1_out, multiplexer_2_out, multiplexer_3_out, n1_to_16_bit_1_out_2, n1_to_16_bit_2_out_2,
       n1_to_16_bit_3_out_2, n1_to_16_bit_4_out_2, n1_to_16_bit_5_out_2, n1_to_16_bit_6_out_2,
       n1_to_16_bit_7_out_2, Val_1_q, Val_2_q;

  Comparator #(.width(16)) comparator_1 (.a({16{1'b0}}), .b(sub_instruction), .eq(comparator_1_eq));  // open: gt, lt
  Comparator #(.width(16)) comparator_2 (.a(16'h1), .b(sub_instruction), .eq(comparator_2_eq));  // open: gt, lt
  Comparator #(.width(16)) comparator_3 (
    .a(16'h2), .b(sub_instruction), .eq(comparator_3_eq), .lt(mem_addr));  // open: gt
  _1_to_16_bit u_1_to_16_bit_1 (.in_1(comparator_1_eq), .out_2(n1_to_16_bit_1_out_2));
  _1_to_16_bit u_1_to_16_bit_2 (.in_1(comparator_2_eq), .out_2(n1_to_16_bit_2_out_2));
  _1_to_16_bit u_1_to_16_bit_3 (.in_1(comparator_3_eq), .out_2(n1_to_16_bit_3_out_2));
  assign and_1_out = data & n1_to_16_bit_1_out_2;  // AND_Gate and_1, 16 bits wide
  assign and_2_out = data & n1_to_16_bit_2_out_2;  // AND_Gate and_2, 16 bits wide
  assign and_3_out = data & n1_to_16_bit_3_out_2;  // AND_Gate and_3, 16 bits wide
  Multiplexer #(.width(16), .enable("false")) multiplexer_1 (
    .in0(Val_1_q), .in1(and_1_out), .out(multiplexer_1_out), .sel(comparator_1_eq));
  Multiplexer #(.width(16), .enable("false")) multiplexer_2 (
    .in0(Val_2_q), .in1(and_2_out), .out(multiplexer_2_out), .sel(comparator_2_eq));
  Multiplexer #(.width(16), .enable("false")) multiplexer_3 (
    .in0(Jump_to_reg_q), .in1(and_3_out), .out(multiplexer_3_out), .sel(comparator_3_eq));
  Register #(.width(16)) Val_1 (.D(multiplexer_1_out), .Q(Val_1_q), .clk(clock), .clr(reset));  // open: en
  Register #(.width(16)) Val_2 (.D(multiplexer_2_out), .Q(Val_2_q), .clk(clock), .clr(reset));  // open: en
  Register #(.width(16)) Jump_to_reg (.D(multiplexer_3_out), .Q(Jump_to_reg_q), .clk(clock), .clr(reset));  // open: en
  Comparator #(.width(16)) comparator_4 (.a(16'h3), .b(sub_instruction), .eq(value_1));  // open: gt, lt
  Comparator #(.width(16)) comparator_5 (.a(16'h4), .b(sub_instruction), .eq(value_2));  // open: gt, lt
  Comparator #(.width(16)) comparator_6 (.a(16'h6), .b(sub_instruction), .eq(comparator_6_eq));  // open: gt, lt
  Comparator #(.width(16)) comparator_7 (.a(16'h5), .b(sub_instruction), .eq(save_result));  // open: gt, lt
  _1_to_16_bit u_1_to_16_bit_4 (.in_1(value_1), .out_2(n1_to_16_bit_4_out_2));
  _1_to_16_bit u_1_to_16_bit_5 (.in_1(value_2), .out_2(n1_to_16_bit_5_out_2));
  _1_to_16_bit u_1_to_16_bit_6 (.in_1(comparator_6_eq), .out_2(n1_to_16_bit_6_out_2));
  _1_to_16_bit u_1_to_16_bit_7 (.in_1(save_result), .out_2(n1_to_16_bit_7_out_2));
  assign and_4_out = Val_1_q & n1_to_16_bit_4_out_2;  // AND_Gate and_4, 16 bits wide
  assign and_5_out = Val_2_q & n1_to_16_bit_5_out_2;  // AND_Gate and_5, 16 bits wide
  assign and_6_out = Jump_to_reg_q & n1_to_16_bit_6_out_2;  // AND_Gate and_6, 16 bits wide
  assign and_7_out = Val_1_q & n1_to_16_bit_7_out_2;  // AND_Gate and_7, 16 bits wide
  assign out_5 = and_4_out | and_5_out | and_6_out | and_7_out;  // OR_Gate or_1, 16 bits wide
endmodule

module _1_to_16_bit (
  input  in_1,
  output [15:0] out_2
);


  assign out_2 = {16{in_1}};
endmodule

module LEQ_zero (
  input  [15:0] in_1,
  output out_2
);

  wire comparator_1_eq;

  Comparator #(.width(16)) comparator_1 (.a({16{1'b0}}), .b(in_1), .eq(comparator_1_eq));  // open: gt, lt
  or or_1 (out_2, comparator_1_eq, in_1[15]);
endmodule

// ROM
module bootloader (
  input  clock,
  input  reset,
  output [15:0] Address,
  output [15:0] Data,
  output Write_ram,
  output unlock_system,
  output [15:0] Prog_Length
);

  wire and_1_out, comparator_1_eq, comparator_1_lt, comparator_2_eq, comparator_2_lt, not_1_out, not_2_out,
       or_1_out;
  wire [15:0] counter_1_q, multiplexer_1_out;

  and and_1 (and_1_out, 1'b1, not_1_out);
  Counter #(.width(16), .max('hffff)) counter_1 (
    .load(1'b0), .count(and_1_out), .Q(counter_1_q), .clk(clock));  // open: D, carry, clr
  not not_1 (not_1_out, unlock_system);
  Multiplexer #(.width(16), .enable("false")) multiplexer_1 (
    .in0(Data), .in1(Prog_Length), .out(multiplexer_1_out), .sel(comparator_2_lt));
  ROM #(.addrWidth(16), .dataWidth(16)) rom_1 (.addr(counter_1_q), .data(Data), .sel(not_1_out));
  Register #(.width(16)) register_1 (.D(multiplexer_1_out), .Q(Prog_Length), .clk(clock), .clr(reset));  // open: en
  Comparator #(.width(16)) comparator_1 (
    .a(counter_1_q), .b(Prog_Length), .gt(unlock_system), .eq(comparator_1_eq), .lt(comparator_1_lt));
  Comparator #(.width(16)) comparator_2 (
    .a({16{1'b0}}), .b(Prog_Length), .eq(comparator_2_eq), .lt(comparator_2_lt));  // open: gt
  or or_1 (or_1_out, comparator_1_eq, comparator_1_lt);
  not not_2 (not_2_out, comparator_2_eq);
  Subtractor #(.width(16)) subtractor_1 (.a(counter_1_q), .b(16'h1), .out(Address));  // open: bin, bout
  and and_2 (Write_ram, not_2_out, or_1_out);

  // Notes on the sheet:
  //   contents of rom_1 (hex, n*v repeats v):
  //   87 5d 5d 3 5d 62 6 5e 5e 9 5e 63 c 5e 64 f 5e 5e 12 5e 5e 15 5e 5e 18 5f 5f 1b 5e 5e 1e 5e 20 21 5f
  //   5e 24 5e 5e 27 5f 5f 2a 60 60 2d 5f 5f 30 5e 5f 33 5f 5e 36 5f 5e 39 5e 5e 3c 60 5e 3f 5e 5e 42 60
  //   5e 45 60 5e 48 60 65 4b 5f 60 c 86 86 51 5e 5e 54 5e 5d 57 86 5e 5a 61 61 5a 5*0 fffe 0 ffff 1
endmodule

// SFR
module special_function_registers (
  input  [15:0] Prog_Length,
  input  [15:0] address,
  input  [15:0] data_in,
  input  clock,
  input  write_nread,
  input  reset,
  input  Running
);

  wire comparator_1_eq, not_1_out;
  wire [15:0] and_1_out, matrix_driver_1_out_6, matrix_driver_1_out_7, matrix_driver_1_out_8,
       matrix_driver_1_out_9, matrix_driver_1_out_10, matrix_driver_1_out_11, matrix_driver_1_out_12,
       matrix_driver_1_out_13, matrix_driver_1_out_14, matrix_driver_1_out_15, matrix_driver_1_out_16,
       matrix_driver_1_out_17, matrix_driver_1_out_18, matrix_driver_1_out_19, matrix_driver_1_out_20,
       matrix_driver_1_out_21, matrix_driver_1_out_22, matrix_driver_1_out_23, matrix_driver_1_out_24,
       matrix_driver_1_out_25, matrix_driver_1_out_26, matrix_driver_1_out_27, matrix_driver_1_out_28,
       matrix_driver_1_out_29, matrix_driver_1_out_30, matrix_driver_1_out_31, matrix_driver_1_out_32,
       matrix_driver_1_out_33, matrix_driver_1_out_34, matrix_driver_1_out_35, matrix_driver_1_out_36,
       matrix_driver_1_out_37, multiplexer_1_out, register_1_q, subtractor_1_out;

  LED led_1 (.in(not_1_out));
  not not_1 (not_1_out, Running);
  LED led_2 (.in(Running));
  Subtractor #(.width(16)) subtractor_1 (.a(Prog_Length), .b(16'h1), .out(subtractor_1_out));  // open: bin, bout
  assign and_1_out = address & {16{write_nread}};  // AND_Gate and_1, 16 bits wide
  Comparator #(.width(16)) comparator_1 (.a(and_1_out), .b(subtractor_1_out), .eq(comparator_1_eq));  // open: gt, lt
  Multiplexer #(.width(16)) multiplexer_1 (
    .in0(register_1_q), .in1(data_in), .out(multiplexer_1_out), .sel(comparator_1_eq));  // open: en
  Register #(.width(16)) register_1 (.D(multiplexer_1_out), .Q(register_1_q), .clk(clock), .clr(reset));  // open: en
  DotMatrix #(.matrixcols(32), .matrixrows(16)) dotmatrix_1 (
    .col0(matrix_driver_1_out_6), .col1(matrix_driver_1_out_7), .col2(matrix_driver_1_out_8),
    .col3(matrix_driver_1_out_9), .col4(matrix_driver_1_out_10), .col5(matrix_driver_1_out_11),
    .col6(matrix_driver_1_out_12), .col7(matrix_driver_1_out_13), .col8(matrix_driver_1_out_14),
    .col9(matrix_driver_1_out_15), .col10(matrix_driver_1_out_16), .col11(matrix_driver_1_out_17),
    .col12(matrix_driver_1_out_18), .col13(matrix_driver_1_out_19), .col14(matrix_driver_1_out_20),
    .col15(matrix_driver_1_out_21), .col16(matrix_driver_1_out_22), .col17(matrix_driver_1_out_23),
    .col18(matrix_driver_1_out_24), .col19(matrix_driver_1_out_25), .col20(matrix_driver_1_out_26),
    .col21(matrix_driver_1_out_27), .col22(matrix_driver_1_out_28), .col23(matrix_driver_1_out_29),
    .col24(matrix_driver_1_out_30), .col25(matrix_driver_1_out_31), .col26(matrix_driver_1_out_32),
    .col27(matrix_driver_1_out_33), .col28(matrix_driver_1_out_34), .col29(matrix_driver_1_out_35),
    .col30(matrix_driver_1_out_36), .col31(matrix_driver_1_out_37));
  matrix_driver matrix_driver_1 (
    .Prog_Length(subtractor_1_out), .address(and_1_out), .data(data_in), .reset(reset), .clock(clock),
    .out_6(matrix_driver_1_out_6), .out_7(matrix_driver_1_out_7), .out_8(matrix_driver_1_out_8),
    .out_9(matrix_driver_1_out_9), .out_10(matrix_driver_1_out_10), .out_11(matrix_driver_1_out_11),
    .out_12(matrix_driver_1_out_12), .out_13(matrix_driver_1_out_13), .out_14(matrix_driver_1_out_14),
    .out_15(matrix_driver_1_out_15), .out_16(matrix_driver_1_out_16), .out_17(matrix_driver_1_out_17),
    .out_18(matrix_driver_1_out_18), .out_19(matrix_driver_1_out_19), .out_20(matrix_driver_1_out_20),
    .out_21(matrix_driver_1_out_21), .out_22(matrix_driver_1_out_22), .out_23(matrix_driver_1_out_23),
    .out_24(matrix_driver_1_out_24), .out_25(matrix_driver_1_out_25), .out_26(matrix_driver_1_out_26),
    .out_27(matrix_driver_1_out_27), .out_28(matrix_driver_1_out_28), .out_29(matrix_driver_1_out_29),
    .out_30(matrix_driver_1_out_30), .out_31(matrix_driver_1_out_31), .out_32(matrix_driver_1_out_32),
    .out_33(matrix_driver_1_out_33), .out_34(matrix_driver_1_out_34), .out_35(matrix_driver_1_out_35),
    .out_36(matrix_driver_1_out_36), .out_37(matrix_driver_1_out_37));
  Hex_Digit_Display hex_digit_display_1 (.value(register_1_q[15:12]));  // open: dp
  Hex_Digit_Display hex_digit_display_2 (.value(register_1_q[11:8]));  // open: dp
  Hex_Digit_Display hex_digit_display_3 (.value(register_1_q[7:4]));  // open: dp
  Hex_Digit_Display hex_digit_display_4 (.value(register_1_q[3:0]));  // open: dp

  // Notes on the sheet:
  //   Loading Program
  //   Running Program
  //   RETURN VALUE
  //   DISPLAY OUTPUT
endmodule

// MATRIX DRIVER
module matrix_driver (
  input  [15:0] Prog_Length,
  input  [15:0] address,
  input  [15:0] data,
  input  reset,
  input  clock,
  output [15:0] out_6,
  output [15:0] out_7,
  output [15:0] out_8,
  output [15:0] out_9,
  output [15:0] out_10,
  output [15:0] out_11,
  output [15:0] out_12,
  output [15:0] out_13,
  output [15:0] out_14,
  output [15:0] out_15,
  output [15:0] out_16,
  output [15:0] out_17,
  output [15:0] out_18,
  output [15:0] out_19,
  output [15:0] out_20,
  output [15:0] out_21,
  output [15:0] out_22,
  output [15:0] out_23,
  output [15:0] out_24,
  output [15:0] out_25,
  output [15:0] out_26,
  output [15:0] out_27,
  output [15:0] out_28,
  output [15:0] out_29,
  output [15:0] out_30,
  output [15:0] out_31,
  output [15:0] out_32,
  output [15:0] out_33,
  output [15:0] out_34,
  output [15:0] out_35,
  output [15:0] out_36,
  output [15:0] out_37
);

  wire comparator_1_eq, comparator_2_eq, comparator_3_eq, comparator_4_eq, comparator_5_eq, comparator_6_eq,
       comparator_7_eq, comparator_8_eq, comparator_9_eq, comparator_10_eq, comparator_11_eq,
       comparator_12_eq, comparator_13_eq, comparator_14_eq, comparator_15_eq, comparator_16_eq,
       comparator_17_eq, comparator_18_eq, comparator_19_eq, comparator_20_eq, comparator_21_eq,
       comparator_22_eq, comparator_23_eq, comparator_24_eq, comparator_25_eq, comparator_26_eq,
       comparator_27_eq, comparator_28_eq, comparator_29_eq, comparator_30_eq, comparator_31_eq,
       comparator_32_eq;
  wire [15:0] multiplexer_1_out, multiplexer_2_out, multiplexer_3_out, multiplexer_4_out, multiplexer_5_out,
       multiplexer_6_out, multiplexer_7_out, multiplexer_8_out, multiplexer_9_out, multiplexer_10_out,
       multiplexer_11_out, multiplexer_12_out, multiplexer_13_out, multiplexer_14_out, multiplexer_15_out,
       multiplexer_16_out, multiplexer_17_out, multiplexer_18_out, multiplexer_19_out, multiplexer_20_out,
       multiplexer_21_out, multiplexer_22_out, multiplexer_23_out, multiplexer_24_out, multiplexer_25_out,
       multiplexer_26_out, multiplexer_27_out, multiplexer_28_out, multiplexer_29_out, multiplexer_30_out,
       multiplexer_31_out, multiplexer_32_out, subtractor_1_out, subtractor_2_out, subtractor_3_out,
       subtractor_4_out, subtractor_5_out, subtractor_6_out, subtractor_7_out, subtractor_8_out,
       subtractor_9_out, subtractor_10_out, subtractor_11_out, subtractor_12_out, subtractor_13_out,
       subtractor_14_out, subtractor_15_out, subtractor_16_out, subtractor_17_out, subtractor_18_out,
       subtractor_19_out, subtractor_20_out, subtractor_21_out, subtractor_22_out, subtractor_23_out,
       subtractor_24_out, subtractor_25_out, subtractor_26_out, subtractor_27_out, subtractor_28_out,
       subtractor_29_out, subtractor_30_out, subtractor_31_out, subtractor_32_out;

  Subtractor #(.width(16)) subtractor_1 (.a(Prog_Length), .b(16'h1), .out(subtractor_1_out));  // open: bin, bout
  Comparator #(.width(16)) comparator_1 (.a(subtractor_1_out), .b(address), .eq(comparator_1_eq));  // open: gt, lt
  Subtractor #(.width(16)) subtractor_2 (.a(subtractor_1_out), .b(16'h1), .out(subtractor_2_out));  // open: bin, bout
  Register #(.width(16)) register_1 (.D(multiplexer_1_out), .Q(out_6), .clk(clock), .clr(reset));  // open: en
  Multiplexer #(.width(16)) multiplexer_1 (
    .in0(out_6), .in1(data), .out(multiplexer_1_out), .sel(comparator_1_eq));  // open: en
  Comparator #(.width(16)) comparator_2 (.a(subtractor_2_out), .b(address), .eq(comparator_2_eq));  // open: gt, lt
  Subtractor #(.width(16)) subtractor_3 (.a(subtractor_2_out), .b(16'h1), .out(subtractor_3_out));  // open: bin, bout
  Register #(.width(16)) register_2 (.D(multiplexer_2_out), .Q(out_7), .clk(clock), .clr(reset));  // open: en
  Multiplexer #(.width(16)) multiplexer_2 (
    .in0(out_7), .in1(data), .out(multiplexer_2_out), .sel(comparator_2_eq));  // open: en
  Comparator #(.width(16)) comparator_3 (.a(subtractor_3_out), .b(address), .eq(comparator_3_eq));  // open: gt, lt
  Subtractor #(.width(16)) subtractor_4 (.a(subtractor_3_out), .b(16'h1), .out(subtractor_4_out));  // open: bin, bout
  Register #(.width(16)) register_3 (.D(multiplexer_3_out), .Q(out_8), .clk(clock), .clr(reset));  // open: en
  Multiplexer #(.width(16)) multiplexer_3 (
    .in0(out_8), .in1(data), .out(multiplexer_3_out), .sel(comparator_3_eq));  // open: en
  Comparator #(.width(16)) comparator_4 (.a(subtractor_4_out), .b(address), .eq(comparator_4_eq));  // open: gt, lt
  Subtractor #(.width(16)) subtractor_5 (.a(subtractor_4_out), .b(16'h1), .out(subtractor_5_out));  // open: bin, bout
  Multiplexer #(.width(16)) multiplexer_4 (
    .in0(out_9), .in1(data), .out(multiplexer_4_out), .sel(comparator_4_eq));  // open: en
  Register #(.width(16)) register_4 (.D(multiplexer_4_out), .Q(out_9), .clk(clock), .clr(reset));  // open: en
  Comparator #(.width(16)) comparator_5 (.a(subtractor_5_out), .b(address), .eq(comparator_5_eq));  // open: gt, lt
  Subtractor #(.width(16)) subtractor_6 (.a(subtractor_5_out), .b(16'h1), .out(subtractor_6_out));  // open: bin, bout
  Register #(.width(16)) register_5 (.D(multiplexer_5_out), .Q(out_10), .clk(clock), .clr(reset));  // open: en
  Multiplexer #(.width(16)) multiplexer_5 (
    .in0(out_10), .in1(data), .out(multiplexer_5_out), .sel(comparator_5_eq));  // open: en
  Comparator #(.width(16)) comparator_6 (.a(subtractor_6_out), .b(address), .eq(comparator_6_eq));  // open: gt, lt
  Multiplexer #(.width(16)) multiplexer_6 (
    .in0(out_11), .in1(data), .out(multiplexer_6_out), .sel(comparator_6_eq));  // open: en
  Subtractor #(.width(16)) subtractor_7 (.a(subtractor_6_out), .b(16'h1), .out(subtractor_7_out));  // open: bin, bout
  Register #(.width(16)) register_6 (.D(multiplexer_6_out), .Q(out_11), .clk(clock), .clr(reset));  // open: en
  Comparator #(.width(16)) comparator_7 (.a(subtractor_7_out), .b(address), .eq(comparator_7_eq));  // open: gt, lt
  Subtractor #(.width(16)) subtractor_8 (.a(subtractor_7_out), .b(16'h1), .out(subtractor_8_out));  // open: bin, bout
  Register #(.width(16)) register_7 (.D(multiplexer_7_out), .Q(out_12), .clk(clock), .clr(reset));  // open: en
  Multiplexer #(.width(16)) multiplexer_7 (
    .in0(out_12), .in1(data), .out(multiplexer_7_out), .sel(comparator_7_eq));  // open: en
  Comparator #(.width(16)) comparator_8 (.a(subtractor_8_out), .b(address), .eq(comparator_8_eq));  // open: gt, lt
  Multiplexer #(.width(16)) multiplexer_8 (
    .in0(out_13), .in1(data), .out(multiplexer_8_out), .sel(comparator_8_eq));  // open: en
  Subtractor #(.width(16)) subtractor_9 (.a(subtractor_8_out), .b(16'h1), .out(subtractor_9_out));  // open: bin, bout
  Register #(.width(16)) register_8 (.D(multiplexer_8_out), .Q(out_13), .clk(clock), .clr(reset));  // open: en
  Comparator #(.width(16)) comparator_9 (.a(subtractor_9_out), .b(address), .eq(comparator_9_eq));  // open: gt, lt
  Subtractor #(.width(16)) subtractor_10 (.a(subtractor_9_out), .b(16'h1), .out(subtractor_10_out));  // open: bin, bout
  Multiplexer #(.width(16)) multiplexer_9 (
    .in0(out_14), .in1(data), .out(multiplexer_9_out), .sel(comparator_9_eq));  // open: en
  Register #(.width(16)) register_9 (.D(multiplexer_9_out), .Q(out_14), .clk(clock), .clr(reset));  // open: en
  Comparator #(.width(16)) comparator_10 (.a(subtractor_10_out), .b(address), .eq(comparator_10_eq));  // open: gt, lt
  Subtractor #(.width(16)) subtractor_11 (
    .a(subtractor_10_out), .b(16'h1), .out(subtractor_11_out));  // open: bin, bout
  Multiplexer #(.width(16)) multiplexer_10 (
    .in0(out_15), .in1(data), .out(multiplexer_10_out), .sel(comparator_10_eq));  // open: en
  Register #(.width(16)) register_10 (.D(multiplexer_10_out), .Q(out_15), .clk(clock), .clr(reset));  // open: en
  Comparator #(.width(16)) comparator_11 (.a(subtractor_11_out), .b(address), .eq(comparator_11_eq));  // open: gt, lt
  Subtractor #(.width(16)) subtractor_12 (
    .a(subtractor_11_out), .b(16'h1), .out(subtractor_12_out));  // open: bin, bout
  Multiplexer #(.width(16)) multiplexer_11 (
    .in0(out_16), .in1(data), .out(multiplexer_11_out), .sel(comparator_11_eq));  // open: en
  Register #(.width(16)) register_11 (.D(multiplexer_11_out), .Q(out_16), .clk(clock), .clr(reset));  // open: en
  Comparator #(.width(16)) comparator_12 (.a(subtractor_12_out), .b(address), .eq(comparator_12_eq));  // open: gt, lt
  Subtractor #(.width(16)) subtractor_13 (
    .a(subtractor_12_out), .b(16'h1), .out(subtractor_13_out));  // open: bin, bout
  Multiplexer #(.width(16)) multiplexer_12 (
    .in0(out_17), .in1(data), .out(multiplexer_12_out), .sel(comparator_12_eq));  // open: en
  Register #(.width(16)) register_12 (.D(multiplexer_12_out), .Q(out_17), .clk(clock), .clr(reset));  // open: en
  Comparator #(.width(16)) comparator_13 (.a(subtractor_13_out), .b(address), .eq(comparator_13_eq));  // open: gt, lt
  Subtractor #(.width(16)) subtractor_14 (
    .a(subtractor_13_out), .b(16'h1), .out(subtractor_14_out));  // open: bin, bout
  Multiplexer #(.width(16)) multiplexer_13 (
    .in0(out_18), .in1(data), .out(multiplexer_13_out), .sel(comparator_13_eq));  // open: en
  Register #(.width(16)) register_13 (.D(multiplexer_13_out), .Q(out_18), .clk(clock), .clr(reset));  // open: en
  Comparator #(.width(16)) comparator_14 (.a(subtractor_14_out), .b(address), .eq(comparator_14_eq));  // open: gt, lt
  Subtractor #(.width(16)) subtractor_15 (
    .a(subtractor_14_out), .b(16'h1), .out(subtractor_15_out));  // open: bin, bout
  Register #(.width(16)) register_14 (.D(multiplexer_14_out), .Q(out_19), .clk(clock), .clr(reset));  // open: en
  Multiplexer #(.width(16)) multiplexer_14 (
    .in0(out_19), .in1(data), .out(multiplexer_14_out), .sel(comparator_14_eq));  // open: en
  Comparator #(.width(16)) comparator_15 (.a(subtractor_15_out), .b(address), .eq(comparator_15_eq));  // open: gt, lt
  Subtractor #(.width(16)) subtractor_16 (
    .a(subtractor_15_out), .b(16'h1), .out(subtractor_16_out));  // open: bin, bout
  Multiplexer #(.width(16)) multiplexer_15 (
    .in0(out_20), .in1(data), .out(multiplexer_15_out), .sel(comparator_15_eq));  // open: en
  Register #(.width(16)) register_15 (.D(multiplexer_15_out), .Q(out_20), .clk(clock), .clr(reset));  // open: en
  Comparator #(.width(16)) comparator_16 (.a(subtractor_16_out), .b(address), .eq(comparator_16_eq));  // open: gt, lt
  Subtractor #(.width(16)) subtractor_17 (
    .a(subtractor_16_out), .b(16'h1), .out(subtractor_17_out));  // open: bin, bout
  Register #(.width(16)) register_16 (.D(multiplexer_16_out), .Q(out_21), .clk(clock), .clr(reset));  // open: en
  Multiplexer #(.width(16)) multiplexer_16 (
    .in0(out_21), .in1(data), .out(multiplexer_16_out), .sel(comparator_16_eq));  // open: en
  Comparator #(.width(16)) comparator_17 (.a(subtractor_17_out), .b(address), .eq(comparator_17_eq));  // open: gt, lt
  Subtractor #(.width(16)) subtractor_18 (
    .a(subtractor_17_out), .b(16'h1), .out(subtractor_18_out));  // open: bin, bout
  Register #(.width(16)) register_17 (.D(multiplexer_17_out), .Q(out_22), .clk(clock), .clr(reset));  // open: en
  Multiplexer #(.width(16)) multiplexer_17 (
    .in0(out_22), .in1(data), .out(multiplexer_17_out), .sel(comparator_17_eq));  // open: en
  Comparator #(.width(16)) comparator_18 (.a(subtractor_18_out), .b(address), .eq(comparator_18_eq));  // open: gt, lt
  Subtractor #(.width(16)) subtractor_19 (
    .a(subtractor_18_out), .b(16'h1), .out(subtractor_19_out));  // open: bin, bout
  Register #(.width(16)) register_18 (.D(multiplexer_18_out), .Q(out_23), .clk(clock), .clr(reset));  // open: en
  Multiplexer #(.width(16)) multiplexer_18 (
    .in0(out_23), .in1(data), .out(multiplexer_18_out), .sel(comparator_18_eq));  // open: en
  Comparator #(.width(16)) comparator_19 (.a(subtractor_19_out), .b(address), .eq(comparator_19_eq));  // open: gt, lt
  Subtractor #(.width(16)) subtractor_20 (
    .a(subtractor_19_out), .b(16'h1), .out(subtractor_20_out));  // open: bin, bout
  Register #(.width(16)) register_19 (.D(multiplexer_19_out), .Q(out_24), .clk(clock), .clr(reset));  // open: en
  Multiplexer #(.width(16)) multiplexer_19 (
    .in0(out_24), .in1(data), .out(multiplexer_19_out), .sel(comparator_19_eq));  // open: en
  Comparator #(.width(16)) comparator_20 (.a(subtractor_20_out), .b(address), .eq(comparator_20_eq));  // open: gt, lt
  Subtractor #(.width(16)) subtractor_21 (
    .a(subtractor_20_out), .b(16'h1), .out(subtractor_21_out));  // open: bin, bout
  Multiplexer #(.width(16)) multiplexer_20 (
    .in0(out_25), .in1(data), .out(multiplexer_20_out), .sel(comparator_20_eq));  // open: en
  Register #(.width(16)) register_20 (.D(multiplexer_20_out), .Q(out_25), .clk(clock), .clr(reset));  // open: en
  Comparator #(.width(16)) comparator_21 (.a(subtractor_21_out), .b(address), .eq(comparator_21_eq));  // open: gt, lt
  Subtractor #(.width(16)) subtractor_22 (
    .a(subtractor_21_out), .b(16'h1), .out(subtractor_22_out));  // open: bin, bout
  Register #(.width(16)) register_21 (.D(multiplexer_21_out), .Q(out_26), .clk(clock), .clr(reset));  // open: en
  Multiplexer #(.width(16)) multiplexer_21 (
    .in0(out_26), .in1(data), .out(multiplexer_21_out), .sel(comparator_21_eq));  // open: en
  Comparator #(.width(16)) comparator_22 (.a(subtractor_22_out), .b(address), .eq(comparator_22_eq));  // open: gt, lt
  Multiplexer #(.width(16)) multiplexer_22 (
    .in0(out_27), .in1(data), .out(multiplexer_22_out), .sel(comparator_22_eq));  // open: en
  Subtractor #(.width(16)) subtractor_23 (
    .a(subtractor_22_out), .b(16'h1), .out(subtractor_23_out));  // open: bin, bout
  Register #(.width(16)) register_22 (.D(multiplexer_22_out), .Q(out_27), .clk(clock), .clr(reset));  // open: en
  Comparator #(.width(16)) comparator_23 (.a(subtractor_23_out), .b(address), .eq(comparator_23_eq));  // open: gt, lt
  Subtractor #(.width(16)) subtractor_24 (
    .a(subtractor_23_out), .b(16'h1), .out(subtractor_24_out));  // open: bin, bout
  Register #(.width(16)) register_23 (.D(multiplexer_23_out), .Q(out_28), .clk(clock), .clr(reset));  // open: en
  Multiplexer #(.width(16)) multiplexer_23 (
    .in0(out_28), .in1(data), .out(multiplexer_23_out), .sel(comparator_23_eq));  // open: en
  Comparator #(.width(16)) comparator_24 (.a(subtractor_24_out), .b(address), .eq(comparator_24_eq));  // open: gt, lt
  Multiplexer #(.width(16)) multiplexer_24 (
    .in0(out_29), .in1(data), .out(multiplexer_24_out), .sel(comparator_24_eq));  // open: en
  Subtractor #(.width(16)) subtractor_25 (
    .a(subtractor_24_out), .b(16'h1), .out(subtractor_25_out));  // open: bin, bout
  Register #(.width(16)) register_24 (.D(multiplexer_24_out), .Q(out_29), .clk(clock), .clr(reset));  // open: en
  Comparator #(.width(16)) comparator_25 (.a(subtractor_25_out), .b(address), .eq(comparator_25_eq));  // open: gt, lt
  Subtractor #(.width(16)) subtractor_26 (
    .a(subtractor_25_out), .b(16'h1), .out(subtractor_26_out));  // open: bin, bout
  Multiplexer #(.width(16)) multiplexer_25 (
    .in0(out_30), .in1(data), .out(multiplexer_25_out), .sel(comparator_25_eq));  // open: en
  Register #(.width(16)) register_25 (.D(multiplexer_25_out), .Q(out_30), .clk(clock), .clr(reset));  // open: en
  Comparator #(.width(16)) comparator_26 (.a(subtractor_26_out), .b(address), .eq(comparator_26_eq));  // open: gt, lt
  Subtractor #(.width(16)) subtractor_27 (
    .a(subtractor_26_out), .b(16'h1), .out(subtractor_27_out));  // open: bin, bout
  Multiplexer #(.width(16)) multiplexer_26 (
    .in0(out_31), .in1(data), .out(multiplexer_26_out), .sel(comparator_26_eq));  // open: en
  Register #(.width(16)) register_26 (.D(multiplexer_26_out), .Q(out_31), .clk(clock), .clr(reset));  // open: en
  Comparator #(.width(16)) comparator_27 (.a(subtractor_27_out), .b(address), .eq(comparator_27_eq));  // open: gt, lt
  Subtractor #(.width(16)) subtractor_28 (
    .a(subtractor_27_out), .b(16'h1), .out(subtractor_28_out));  // open: bin, bout
  Multiplexer #(.width(16)) multiplexer_27 (
    .in0(out_32), .in1(data), .out(multiplexer_27_out), .sel(comparator_27_eq));  // open: en
  Register #(.width(16)) register_27 (.D(multiplexer_27_out), .Q(out_32), .clk(clock), .clr(reset));  // open: en
  Comparator #(.width(16)) comparator_28 (.a(subtractor_28_out), .b(address), .eq(comparator_28_eq));  // open: gt, lt
  Subtractor #(.width(16)) subtractor_29 (
    .a(subtractor_28_out), .b(16'h1), .out(subtractor_29_out));  // open: bin, bout
  Multiplexer #(.width(16)) multiplexer_28 (
    .in0(out_33), .in1(data), .out(multiplexer_28_out), .sel(comparator_28_eq));  // open: en
  Register #(.width(16)) register_28 (.D(multiplexer_28_out), .Q(out_33), .clk(clock), .clr(reset));  // open: en
  Comparator #(.width(16)) comparator_29 (.a(subtractor_29_out), .b(address), .eq(comparator_29_eq));  // open: gt, lt
  Subtractor #(.width(16)) subtractor_30 (
    .a(subtractor_29_out), .b(16'h1), .out(subtractor_30_out));  // open: bin, bout
  Multiplexer #(.width(16)) multiplexer_29 (
    .in0(out_34), .in1(data), .out(multiplexer_29_out), .sel(comparator_29_eq));  // open: en
  Register #(.width(16)) register_29 (.D(multiplexer_29_out), .Q(out_34), .clk(clock), .clr(reset));  // open: en
  Comparator #(.width(16)) comparator_30 (.a(subtractor_30_out), .b(address), .eq(comparator_30_eq));  // open: gt, lt
  Subtractor #(.width(16)) subtractor_31 (
    .a(subtractor_30_out), .b(16'h1), .out(subtractor_31_out));  // open: bin, bout
  Multiplexer #(.width(16)) multiplexer_30 (
    .in0(out_35), .in1(data), .out(multiplexer_30_out), .sel(comparator_30_eq));  // open: en
  Register #(.width(16)) register_30 (.D(multiplexer_30_out), .Q(out_35), .clk(clock), .clr(reset));  // open: en
  Comparator #(.width(16)) comparator_31 (.a(subtractor_31_out), .b(address), .eq(comparator_31_eq));  // open: gt, lt
  Subtractor #(.width(16)) subtractor_32 (
    .a(subtractor_31_out), .b(16'h1), .out(subtractor_32_out));  // open: bin, bout
  Multiplexer #(.width(16)) multiplexer_31 (
    .in0(out_36), .in1(data), .out(multiplexer_31_out), .sel(comparator_31_eq));  // open: en
  Register #(.width(16)) register_31 (.D(multiplexer_31_out), .Q(out_36), .clk(clock), .clr(reset));  // open: en
  Comparator #(.width(16)) comparator_32 (.a(subtractor_32_out), .b(address), .eq(comparator_32_eq));  // open: gt, lt
  Subtractor #(.width(16)) subtractor_33 (.a(subtractor_32_out), .b(16'h1));  // open: out, bin, bout
  Multiplexer #(.width(16)) multiplexer_32 (
    .in0(out_37), .in1(data), .out(multiplexer_32_out), .sel(comparator_32_eq));  // open: en
  Register #(.width(16)) register_32 (.D(multiplexer_32_out), .Q(out_37), .clk(clock), .clr(reset));  // open: en
endmodule
